// Logisim project RCLA.circ as structural Verilog: 13 circuits, main circuit full_adder
module main (
  input  in_1,
  input  [31:0] A_hex,
  input  [31:0] B_hex,
  output [31:0] Sum1_hex,
  output [31:0] Sum2_hex
);

  wire n32bit_hybridrcla_1_overflow, n32bitrca_1_co;

  Hex_Digit_Display hex_digit_display_1 (.value(A_hex[3:0]));  // open: dp
  Hex_Digit_Display hex_digit_display_2 (.value(A_hex[7:4]));  // open: dp
  _32bit_hybridRCLA u_32bit_hybridrcla_1 (
    .add_subtract(in_1), .A(A_hex), .B(B_hex), .overflow(n32bit_hybridrcla_1_overflow), .Sum(Sum1_hex));
  LED overflow (.in(n32bit_hybridrcla_1_overflow));
  Hex_Digit_Display hex_digit_display_3 (.value(A_hex[15:12]));  // open: dp
  Hex_Digit_Display hex_digit_display_4 (.value(A_hex[11:8]));  // open: dp
  Hex_Digit_Display hex_digit_display_5 (.value(A_hex[19:16]));  // open: dp
  Hex_Digit_Display hex_digit_display_6 (.value(A_hex[23:20]));  // open: dp
  Hex_Digit_Display hex_digit_display_7 (.value(Sum1_hex[3:0]));  // open: dp
  Hex_Digit_Display hex_digit_display_8 (.value(A_hex[31:28]));  // open: dp
  Hex_Digit_Display hex_digit_display_9 (.value(A_hex[27:24]));  // open: dp
  Hex_Digit_Display hex_digit_display_10 (.value(Sum1_hex[7:4]));  // open: dp
  Hex_Digit_Display hex_digit_display_11 (.value(Sum1_hex[11:8]));  // open: dp
  Hex_Digit_Display hex_digit_display_12 (.value(Sum1_hex[19:16]));  // open: dp
  Hex_Digit_Display hex_digit_display_13 (.value(Sum1_hex[15:12]));  // open: dp
  Hex_Digit_Display hex_digit_display_14 (.value(Sum1_hex[27:24]));  // open: dp
  Hex_Digit_Display hex_digit_display_15 (.value(Sum1_hex[23:20]));  // open: dp
  Hex_Digit_Display hex_digit_display_16 (.value(B_hex[3:0]));  // open: dp
  _32bitRCA u_32bitrca_1 (.add_subtract(in_1), .A(A_hex), .B(B_hex), .Sum(Sum2_hex), .Co(n32bitrca_1_co));
  Hex_Digit_Display hex_digit_display_17 (.value(Sum1_hex[31:28]));  // open: dp
  Hex_Digit_Display hex_digit_display_18 (.value(B_hex[11:8]));  // open: dp
  Hex_Digit_Display hex_digit_display_19 (.value(B_hex[7:4]));  // open: dp
  LED overflow_2 (.in(n32bitrca_1_co));
  Hex_Digit_Display hex_digit_display_20 (.value(B_hex[15:12]));  // open: dp
  Hex_Digit_Display hex_digit_display_21 (.value(B_hex[19:16]));  // open: dp
  Hex_Digit_Display hex_digit_display_22 (.value(B_hex[27:24]));  // open: dp
  Hex_Digit_Display hex_digit_display_23 (.value(B_hex[23:20]));  // open: dp
  Hex_Digit_Display hex_digit_display_24 (.value(Sum2_hex[3:0]));  // open: dp
  Hex_Digit_Display hex_digit_display_25 (.value(Sum2_hex[7:4]));  // open: dp
  Hex_Digit_Display hex_digit_display_26 (.value(B_hex[31:28]));  // open: dp
  Hex_Digit_Display hex_digit_display_27 (.value(Sum2_hex[15:12]));  // open: dp
  Hex_Digit_Display hex_digit_display_28 (.value(Sum2_hex[11:8]));  // open: dp
  Hex_Digit_Display hex_digit_display_29 (.value(Sum2_hex[19:16]));  // open: dp
  Hex_Digit_Display hex_digit_display_30 (.value(Sum2_hex[23:20]));  // open: dp
  Hex_Digit_Display hex_digit_display_31 (.value(Sum2_hex[31:28]));  // open: dp
  Hex_Digit_Display hex_digit_display_32 (.value(Sum2_hex[27:24]));  // open: dp
endmodule

// FA
module full_adder (
  input  Ci,
  input  A,
  input  B,
  output Sum,
  output Co
);

  wire and_1_out, and_2_out, xor_1_out;

  xor xor_1 (xor_1_out, A, B);
  and and_1 (and_1_out, A, B);
  xor xor_2 (Sum, xor_1_out, Ci);
  and and_2 (and_2_out, xor_1_out, Ci);
  or or_1 (Co, and_2_out, and_1_out);
endmodule

// RCLG
module _2bit_RCLG (
  input  C0,
  input  P0,
  input  G0,
  input  P1,
  input  G1,
  output C0_2,
  output P0_2,
  output C1,
  output P1_2,
  output C2
);

  wire and_1_out, and_2_out, and_3_out;

  and and_1 (and_1_out, C0, P0, P1);
  and and_2 (and_2_out, G0, P1);
  and and_3 (and_3_out, C0, P1);
  or or_1 (C2, and_1_out, and_2_out, G1);
  or or_2 (C1, and_3_out, G0);

  assign C0_2 = C0;
  assign P0_2 = P0;
  assign P1_2 = P1;
endmodule

module _4bit_RCLA (
  input  [3:0] A,
  input  [3:0] B,
  input  Ci,
  output Co,
  output [3:0] Sum
);

  wire n4bitpggen_1_g0, n4bitpggen_1_g1, n4bitpggen_1_g2, n4bitpggen_1_g3, n4bitpggen_1_p0, n4bitpggen_1_p1,
       n4bitpggen_1_p2, n4bitpggen_1_p3, n4bitrclg_1_c0, n4bitrclg_1_c1, n4bitrclg_1_c2, n4bitrclg_1_c3,
       n4bitrclg_1_c4, n4bitrclg_1_p0_2, n4bitrclg_1_p1_2, n4bitrclg_1_p2_2, n4bitrclg_1_p3_2;

  _4bitPGGen u_4bitpggen_1 (
    .P3(n4bitpggen_1_p3), .P2(n4bitpggen_1_p2), .P1(n4bitpggen_1_p1), .P0(n4bitpggen_1_p0),
    .G3(n4bitpggen_1_g3), .G2(n4bitpggen_1_g2), .G1(n4bitpggen_1_g1), .G0(n4bitpggen_1_g0), .A(A), .B(B));
  _4bitRCLG u_4bitrclg_1 (
    .C0(n4bitrclg_1_c0), .P0_2(n4bitrclg_1_p0_2), .C1(n4bitrclg_1_c1), .P1_2(n4bitrclg_1_p1_2),
    .C2(n4bitrclg_1_c2), .P2_2(n4bitrclg_1_p2_2), .C3(n4bitrclg_1_c3), .P3_2(n4bitrclg_1_p3_2),
    .C4(n4bitrclg_1_c4), .Co(Ci), .P0(n4bitpggen_1_p0), .G0(n4bitpggen_1_g0), .P1(n4bitpggen_1_p1),
    .G1(n4bitpggen_1_g1), .P2(n4bitpggen_1_p2), .G2(n4bitpggen_1_g2), .P3(n4bitpggen_1_p3),
    .G3(n4bitpggen_1_g3));
  xor xor_1 (Co, n4bitrclg_1_c4, n4bitrclg_1_c3);
  xor xor_2 (Sum[3], n4bitrclg_1_p3_2, n4bitrclg_1_c3);
  xor xor_3 (Sum[2], n4bitrclg_1_p2_2, n4bitrclg_1_c2);
  xor xor_4 (Sum[1], n4bitrclg_1_p1_2, n4bitrclg_1_c1);
  xor xor_5 (Sum[0], n4bitrclg_1_p0_2, n4bitrclg_1_c0);

  // Notes on the sheet:
  //   Ci xor Pi = Si
endmodule

module HA (
  input  A0,
  input  B0,
  output P0,
  output G0
);

  xor xor_1 (P0, A0, B0);
  and and_1 (G0, A0, B0);
endmodule

// PG-Gen
module _4bitPGGen (
  input  [3:0] A,
  input  [3:0] B,
  output P3,
  output G3,
  output P2,
  output G2,
  output P1,
  output G1,
  output P0,
  output G0
);

  HA MSB (.A0(A[3]), .B0(B[3]), .P0(P3), .G0(G3));
  HA ha_1 (.A0(A[2]), .B0(B[2]), .P0(P2), .G0(G2));
  HA ha_2 (.A0(A[1]), .B0(B[1]), .P0(P1), .G0(G1));
  HA LSB (.A0(A[0]), .B0(B[0]), .P0(P0), .G0(G0));

  // Notes on the sheet:
  //   Generates each propogate and generate for a given 4 bit A and B
endmodule

// PG Gen
module _2bit_PG_Gen (
  input  A1,
  input  A0,
  input  B1,
  input  B0,
  output G1,
  output P1,
  output G0,
  output P0
);

  HA MSB (.A0(A1), .B0(B1), .P0(P1), .G0(G1));
  HA ha_1 (.A0(A0), .B0(B0), .P0(P0), .G0(G0));
endmodule

module _4bit_RCA (
  input  Ci,
  input  [3:0] A,
  input  [3:0] B,
  output [3:0] Sum,
  output Co
);

  wire full_adder_1_co, full_adder_2_co, full_adder_3_co, full_adder_4_co;

  full_adder full_adder_1 (.A(A[0]), .B(B[0]), .Sum(Sum[0]), .Ci(Ci), .Co(full_adder_1_co));
  full_adder full_adder_2 (.A(A[1]), .B(B[1]), .Sum(Sum[1]), .Ci(full_adder_1_co), .Co(full_adder_2_co));
  full_adder full_adder_3 (.A(A[2]), .B(B[2]), .Sum(Sum[2]), .Ci(full_adder_2_co), .Co(full_adder_3_co));
  full_adder full_adder_4 (.A(A[3]), .B(B[3]), .Sum(Sum[3]), .Ci(full_adder_3_co), .Co(full_adder_4_co));
  xor xor_1 (Co, full_adder_4_co, full_adder_3_co);
endmodule

// RCA
module _32bitRCA (
  input  add_subtract,
  input  [31:0] A,
  input  [31:0] B,
  output Co,
  output [31:0] Sum
);

  wire n4bit_rca_1_co, n4bit_rca_2_co, n4bit_rca_3_co, n4bit_rca_4_co, n4bit_rca_5_co, n4bit_rca_6_co,
       n4bit_rca_7_co;
  wire [31:0] bit_extender_1_out, xor_1_out;

  assign bit_extender_1_out = {{31{add_subtract}}, add_subtract};  // Bit_Extender bit_extender_1
  assign xor_1_out = bit_extender_1_out ^ B;  // XOR_Gate xor_1, 32 bits wide
  _4bit_RCA u_4bit_rca_1 (.Ci(add_subtract), .A(A[3:0]), .B(xor_1_out[3:0]), .Co(n4bit_rca_1_co), .Sum(Sum[3:0]));
  _4bit_RCA u_4bit_rca_2 (.Ci(n4bit_rca_1_co), .A(A[7:4]), .B(xor_1_out[7:4]), .Co(n4bit_rca_2_co), .Sum(Sum[7:4]));
  _4bit_RCA u_4bit_rca_3 (.Ci(n4bit_rca_2_co), .A(A[11:8]), .B(xor_1_out[11:8]), .Co(n4bit_rca_3_co), .Sum(Sum[11:8]));
  _4bit_RCA u_4bit_rca_4 (
    .Ci(n4bit_rca_3_co), .A(A[15:12]), .B(xor_1_out[15:12]), .Co(n4bit_rca_4_co), .Sum(Sum[15:12]));
  _4bit_RCA u_4bit_rca_5 (
    .Ci(n4bit_rca_4_co), .A(A[19:16]), .B(xor_1_out[19:16]), .Co(n4bit_rca_5_co), .Sum(Sum[19:16]));
  _4bit_RCA u_4bit_rca_6 (
    .Ci(n4bit_rca_5_co), .A(A[23:20]), .B(xor_1_out[23:20]), .Co(n4bit_rca_6_co), .Sum(Sum[23:20]));
  _4bit_RCA u_4bit_rca_7 (
    .Ci(n4bit_rca_6_co), .A(A[27:24]), .B(xor_1_out[27:24]), .Co(n4bit_rca_7_co), .Sum(Sum[27:24]));
  _4bit_RCA u_4bit_rca_8 (.Ci(n4bit_rca_7_co), .A(A[31:28]), .B(xor_1_out[31:28]), .Co(Co), .Sum(Sum[31:28]));

  // Notes on the sheet:
  //   Regular RCA for comparing efficiency 
endmodule

// FA
module _2bitFA (
  input  Ci,
  input  [1:0] A,
  input  [1:0] B,
  output [1:0] Sum,
  output Co
);

  wire full_adder_1_co;

  full_adder full_adder_1 (.A(A[0]), .B(B[0]), .Sum(Sum[0]), .Ci(Ci), .Co(full_adder_1_co));
  full_adder full_adder_2 (.A(A[1]), .B(B[1]), .Sum(Sum[1]), .Ci(full_adder_1_co), .Co(Co));
endmodule

// 4bit-RCLG
module _4bitRCLG (
  input  Co,
  input  P0,
  input  G0,
  input  P1,
  input  G1,
  input  P2,
  input  G2,
  input  P3,
  input  G3,
  output C0,
  output P0_2,
  output C1,
  output P1_2,
  output C2,
  output P2_2,
  output C3,
  output P3_2,
  output C4
);

  wire and_1_out, and_2_out, and_3_out, and_4_out, and_5_out, and_6_out, and_7_out, and_8_out, and_9_out,
       and_10_out;

  and and_1 (and_1_out, P3, P2, P1, P0, Co);
  and and_2 (and_2_out, P3, P2, P1, G0);
  and and_3 (and_3_out, P2, G1, P3);
  and and_4 (and_4_out, P3, G2);
  and and_5 (and_5_out, Co, P0, P1, P2);
  and and_6 (and_6_out, G0, P1, P2);
  and and_7 (and_7_out, G1, P2);
  and and_8 (and_8_out, Co, P0, P1);
  and and_9 (and_9_out, G0, P1);
  and and_10 (and_10_out, Co, P1);
  or or_1 (C4, and_1_out, and_2_out, and_3_out, and_4_out, G3);
  or or_2 (C3, and_5_out, and_6_out, and_7_out, G2);
  or or_3 (C2, and_8_out, and_9_out, G1);
  or or_4 (C1, and_10_out, G0);

  assign C0 = Co;
  assign P0_2 = P0;
  assign P1_2 = P1;
  assign P2_2 = P2;
  assign P3_2 = P3;

  // Notes on the sheet:
  //   Ci and Pi based on propogate and generate equations
endmodule

// RCLA
module _32bit_hybridRCLA (
  input  add_subtract,
  input  [31:0] A,
  input  [31:0] B,
  output overflow,
  output [31:0] Sum
);

  wire n2bitfa_1_co, n2bitrcla_1_co, n4bit_rcla_1_co, n4bit_rcla_2_co, n4bit_rcla_3_co, n4bit_rcla_4_co,
       n4bit_rcla_5_co, n4bit_rcla_6_co;
  wire [31:0] bit_extender_1_out, xor_1_out;

  assign bit_extender_1_out = {{31{add_subtract}}, add_subtract};  // Bit_Extender bit_extender_1
  assign xor_1_out = bit_extender_1_out ^ B;  // XOR_Gate xor_1, 32 bits wide
  _2bitFA u_2bitfa_1 (.Ci(add_subtract), .A(A[1:0]), .B(xor_1_out[1:0]), .Co(n2bitfa_1_co), .Sum(Sum[1:0]));
  _2bitRCLA u_2bitrcla_1 (.Ci(n2bitfa_1_co), .Co(n2bitrcla_1_co), .A(A[3:2]), .B(xor_1_out[3:2]), .Sum(Sum[3:2]));
  _4bit_RCLA u_4bit_rcla_1 (.A(A[7:4]), .B(xor_1_out[7:4]), .Ci(n2bitrcla_1_co), .Sum(Sum[7:4]), .Co(n4bit_rcla_1_co));
  _4bit_RCLA u_4bit_rcla_2 (
    .A(A[11:8]), .B(xor_1_out[11:8]), .Ci(n4bit_rcla_1_co), .Sum(Sum[11:8]), .Co(n4bit_rcla_2_co));
  _4bit_RCLA u_4bit_rcla_3 (
    .A(A[15:12]), .B(xor_1_out[15:12]), .Ci(n4bit_rcla_2_co), .Sum(Sum[15:12]), .Co(n4bit_rcla_3_co));
  _4bit_RCLA u_4bit_rcla_4 (
    .A(A[19:16]), .B(xor_1_out[19:16]), .Ci(n4bit_rcla_3_co), .Sum(Sum[19:16]), .Co(n4bit_rcla_4_co));
  _4bit_RCLA u_4bit_rcla_5 (
    .A(A[23:20]), .B(xor_1_out[23:20]), .Ci(n4bit_rcla_4_co), .Sum(Sum[23:20]), .Co(n4bit_rcla_5_co));
  _4bit_RCLA u_4bit_rcla_6 (
    .A(A[27:24]), .B(xor_1_out[27:24]), .Ci(n4bit_rcla_5_co), .Sum(Sum[27:24]), .Co(n4bit_rcla_6_co));
  _4bit_RCLA u_4bit_rcla_7 (.A(A[31:28]), .B(xor_1_out[31:28]), .Ci(n4bit_rcla_6_co), .Sum(Sum[31:28]), .Co(overflow));

  // Notes on the sheet:
  //   Optimum 32 bit hybrid RCLA as described in:
  //   two bit full adder
  //   two bit RCLA
  //   Balasubramanian, Padmanabhan, and Nikos Mastorakis. “Performance Comparison of Carry-Lookahead and Carry-Select Adders Based on Accurate and Approximate Additions.” Mdpi.com, 2 Dec. 2016, https://mdpi-res.com/d_attachment/electronics/electronics-07-00369/article_deploy/electronics-07-00369.pdf. 
endmodule

module _2bitRCLA (
  input  [1:0] A,
  input  [1:0] B,
  input  Ci,
  output Co,
  output [1:0] Sum
);

  wire n2bit_pg_gen_1_g0, n2bit_pg_gen_1_g1, n2bit_pg_gen_1_p0, n2bit_pg_gen_1_p1, n2bit_rclg_1_c0_2,
       n2bit_rclg_1_c1, n2bit_rclg_1_p0_2, n2bit_rclg_1_p1_2;

  _2bit_PG_Gen u_2bit_pg_gen_1 (
    .P1(n2bit_pg_gen_1_p1), .G1(n2bit_pg_gen_1_g1), .P0(n2bit_pg_gen_1_p0), .G0(n2bit_pg_gen_1_g0),
    .A0(A[0]), .A1(A[1]), .B1(B[1]), .B0(B[0]));
  _2bit_RCLG u_2bit_rclg_1 (
    .C0_2(n2bit_rclg_1_c0_2), .P0_2(n2bit_rclg_1_p0_2), .C1(n2bit_rclg_1_c1), .P1_2(n2bit_rclg_1_p1_2),
    .C2(Co), .G1(n2bit_pg_gen_1_g1), .P1(n2bit_pg_gen_1_p1), .G0(n2bit_pg_gen_1_g0), .P0(n2bit_pg_gen_1_p0),
    .C0(Ci));
  xor xor_1 (Sum[1], n2bit_rclg_1_p1_2, n2bit_rclg_1_c1);
  xor xor_2 (Sum[0], n2bit_rclg_1_p0_2, n2bit_rclg_1_c0_2);

  // Notes on the sheet:
  //   Two bit RCLA for optimized architecture of full RCLA
endmodule
